# Fritzing sketch rotary (saved by Fritzing 0.9.3b)
breadboards: 1

parts:
  Rotary-Encoder = Rotary Encoder [package=THT]
  Raspberry_Pi_B_rev1 = Raspberry Pi B rev1
  Rotary-Encoder-Switch = SWITCH-MOMENTARY-2 [package=tactile_switch_smd-2]

nets:
  N1: Rotary-Encoder.EncoderPinA, Raspberry_Pi_B_rev1.GPIO_10
  N2: Rotary-Encoder.EncoderPinC, Raspberry_Pi_B_rev1.GND, Rotary-Encoder-Switch.1
  N3: Rotary-Encoder.EncoderPinB, Raspberry_Pi_B_rev1.GPIO_9
  N4: Raspberry_Pi_B_rev1.GPIO_11, Rotary-Encoder-Switch.2
